# Fritzing sketch esquema montagem balança (saved by Fritzing 0.8.7b)
circuit board: 8.46667cm x 5.64444cm
breadboards: 1

parts:
  upper_left = Load Sensor - 50kg [part_number=SEN-10245]
  U1 = NodeMCU V3.0
  Componente1 = HX711 Weighing Sensor Module
  upper_right = Load Sensor - 50kg [part_number=SEN-10245]
  lower_left = Load Sensor - 50kg [part_number=SEN-10245]
  lower_right = Load Sensor - 50kg [part_number=SEN-10245]
  BAT1 = BC9VPC [package=bc9vpc]
  DHT1 = DHT11 Humitidy and Temperature Sensor  # not connected

nets:
  N1: upper_left.B, lower_left.B
  N2: upper_left.W, lower_left.W
  N3: upper_left.R, Componente1.E-
  N4: U1.D2, Componente1.CK/TX
  N5: U1.D3, Componente1.DO/RX
  N6: Componente1.VCC, BAT1.V+
  N7: Componente1.GND, BAT1.V-
  N8: Componente1.E+, lower_right.R
  N9: Componente1.A+, lower_left.R
  N10: Componente1.A-, upper_right.R
  N11: upper_right.B, lower_right.B
  N12: upper_right.W, lower_right.W

custom parts:
  Load Sensor - 50kg: Half-wheatstone bridge Load Cell modified from the Fritzing Repo This load sensor, sometimes called a strain gauge, is the same one found in digital bathroom scales (you know, the ones you use in January for your New Year's resolutions, and then forget about a month later). This sensor can measure up to about 110 pounds.
  NodeMCU V3.0: ESP8266 based NodeMCU
  DHT11 Humitidy and Temperature Sensor: DHT11 Humidity and Temperature Sensor
